# Fritzing sketch park_sensoru (saved by Fritzing 0.9.3b)
breadboards: 1

parts:
  Part1 = Arduino Uno (Rev3)
  R1 = Rotary Potentiometer (Small) [maximum_resistance=100kΩ package=THT]
  R2 = Resistor [tolerance=±5% resistance=220 package=THT]
  LCD1 = LCD screen
  J1 = Piezo Speaker
  R3 = Resistor [tolerance=±5% resistance=220 package=THT]
  hc-sr1 = hc-sr04

nets:
  N1: Part1.D8, hc-sr1.Trig
  N2: Part1.D9_PWM, hc-sr1.Echo
  N3: Part1.D10_PWM/SS, R3.Pin_0
  N4: Part1.D11_PWM/MOSI, LCD1.E
  N5: Part1.D12/MISO, LCD1.RS
  GND: Part1.GND, R1.leg1, LCD1.VSS, LCD1.R/W, LCD1.LED-, J1.pin2, hc-sr1.GND
  N6: Part1.D2, LCD1.DB7
  N7: Part1.D3_PWM, LCD1.DB6
  N8: Part1.D4, LCD1.DB5
  N9: Part1.D5_PWM, LCD1.DB4
  5V: Part1.5V, R1.leg2, R2.Pin_0, LCD1.VDD, hc-sr1.VCC
  N10: R1.wiper, LCD1.V0
  N11: R2.Pin_1, LCD1.LED+
  N12: J1.pin1, R3.Pin_1
